# Fritzing sketch fountain (saved by Fritzing 0.9.3b)
breadboards: 1

parts:
  Raspberry_Pi_1 = Raspberry Pi 3 [part_number=RPI-3-V1.2]
  Q3 = NPN-Transistor [package="TO92 [THT]"]
  M1 = DC Motor

nets:
  N1: Raspberry_Pi_1.GPIO17, Q3.B
  N2: Raspberry_Pi_1.GND, Q3.E
  N3: Q3.C, M1.pin_2
