# Fritzing sketch fountain_arduino (saved by Fritzing 0.9.3b)
breadboards: 1

parts:
  Q3 = NPN-Transistor [package="TO92 [THT]"]
  R1 = Resistor [tolerance=±5% resistance=330 package="2512 [SMD]"]
  D1 = Rectifier Diode [package="Melf DO-213 AA [SMD]"]
  M1 = DC Motor
  Q4 = NPN-Transistor [package="TO92 [THT]"]
  R2 = Resistor [tolerance=±5% resistance=330 package="2512 [SMD]"]
  D2 = Rectifier Diode [package="Melf DO-213 AA [SMD]"]
  M2 = DC Motor
  Q5 = NPN-Transistor [package="TO92 [THT]"]
  R3 = Resistor [tolerance=±5% resistance=330 package="2512 [SMD]"]
  D3 = Rectifier Diode [package="Melf DO-213 AA [SMD]"]
  M3 = DC Motor
  LED1 = RGB LED (com. cathode, rgb) [package="5 mm [THT]"]
  R4 = Resistor [tolerance=±5% resistance=220 package="2512 [SMD]"]
  R5 = Resistor [tolerance=±5% resistance=220 package="2512 [SMD]"]
  R6 = Resistor [tolerance=±5% resistance=220 package="2512 [SMD]"]
  R7 = Resistor [tolerance=±5% resistance=220 package="2512 [SMD]"]
  R8 = Resistor [tolerance=±5% resistance=220 package="2512 [SMD]"]
  R9 = Resistor [tolerance=±5% resistance=220 package="2512 [SMD]"]
  LED2 = RGB LED (com. cathode, rgb) [package="5 mm [THT]"]
  R10 = Resistor [tolerance=±5% resistance=220 package="2512 [SMD]"]
  R11 = Resistor [tolerance=±5% resistance=220 package="2512 [SMD]"]
  R12 = Resistor [tolerance=±5% resistance=220 package="2512 [SMD]"]
  LED3 = RGB LED (com. cathode, rgb) [package="5 mm [THT]"]
  Part1 = Arduino Uno (Rev3)

nets:
  N1: Q3.E, Q4.E, Q5.E, LED1.common_cathode, LED2.common_cathode, LED3.common_cathode, Part1.GND
  N2: Q3.B, R1.Pin_0
  N3: Q3.C, D1.anode, M1.pin_2
  N4: R1.Pin_1, Part1.D11_PWM/MOSI
  N5: D1.cathode, M1.pin_1, D2.cathode, M2.pin_1, D3.cathode, M3.pin_1, Part1.5V
  N6: Q4.B, R2.Pin_0
  N7: Q4.C, D2.anode, M2.pin_2
  N8: R2.Pin_1, Part1.D10_PWM/SS
  N9: Q5.B, R3.Pin_0
  N10: Q5.C, D3.anode, M3.pin_2
  N11: R3.Pin_1, Part1.D9_PWM
  N12: LED1.red_anode, R4.Pin_0
  N13: LED1.green_anode, R5.Pin_0
  N14: LED1.blue_anode, R6.Pin_0
  N15: R4.Pin_1, Part1.D6_PWM
  N16: R5.Pin_1, Part1.D8
  N17: R6.Pin_1, Part1.D7
  N18: R7.Pin_0, LED2.blue_anode
  N19: R7.Pin_1, Part1.D2
  N20: R8.Pin_0, LED2.red_anode
  N21: R8.Pin_1, Part1.D5_PWM
  N22: R9.Pin_0, LED2.green_anode
  N23: R9.Pin_1, Part1.D4
  N24: R10.Pin_0, LED3.blue_anode
  N25: R10.Pin_1, Part1.D0/RX
  N26: R11.Pin_0, LED3.red_anode
  N27: R11.Pin_1, Part1.D3_PWM
  N28: R12.Pin_0, LED3.green_anode
  N29: R12.Pin_1, Part1.D1/TX
