# Fritzing sketch fountain_arduino_shift_register (saved by Fritzing 0.9.3b)
breadboards: 1

parts:
  Q3 = NPN-Transistor [package="TO92 [THT]"]
  R1 = Resistor [tolerance=±5% resistance=330 package="2512 [SMD]"]
  D1 = Rectifier Diode [package="Melf DO-213 AA [SMD]"]
  M1 = DC Motor
  Q4 = NPN-Transistor [package="TO92 [THT]"]
  R2 = Resistor [tolerance=±5% resistance=330 package="2512 [SMD]"]
  D2 = Rectifier Diode [package="Melf DO-213 AA [SMD]"]
  M2 = DC Motor
  Q5 = NPN-Transistor [package="TO92 [THT]"]
  R3 = Resistor [tolerance=±5% resistance=330 package="2512 [SMD]"]
  D3 = Rectifier Diode [package="Melf DO-213 AA [SMD]"]
  M3 = DC Motor
  R10 = Resistor [tolerance=±5% resistance=150 package="2512 [SMD]"]
  R11 = Resistor [tolerance=±5% resistance=220 package="2512 [SMD]"]
  R12 = Resistor [tolerance=±5% resistance=150 package="2512 [SMD]"]
  LED3 = RGB LED (com. cathode, rgb) [package="5 mm [THT]"]
  Part1 = Arduino Uno (Rev3)
  U1 = 74HC595 [package="DIP16 [THT]"]
  U2 = 74HC595 [package="DIP16 [THT]"]
  R13 = Resistor [tolerance=±5% resistance=150 package="2512 [SMD]"]
  R14 = Resistor [tolerance=±5% resistance=220 package="2512 [SMD]"]
  R15 = Resistor [tolerance=±5% resistance=150 package="2512 [SMD]"]
  R16 = Resistor [tolerance=±5% resistance=150 package="2512 [SMD]"]
  R17 = Resistor [tolerance=±5% resistance=220 package="2512 [SMD]"]
  R18 = Resistor [tolerance=±5% resistance=150 package="2512 [SMD]"]
  R19 = Resistor [tolerance=±5% resistance=150 package="2512 [SMD]"]
  R20 = Resistor [tolerance=±5% resistance=220 package="2512 [SMD]"]
  R21 = Resistor [tolerance=±5% resistance=150 package="2512 [SMD]"]
  R22 = Resistor [tolerance=±5% resistance=150 package="2512 [SMD]"]
  R23 = Resistor [tolerance=±5% resistance=220 package="2512 [SMD]"]
  R24 = Resistor [tolerance=±5% resistance=150 package="2512 [SMD]"]
  LED4 = RGB LED (com. cathode, rgb) [package="5 mm [THT]"]
  LED5 = RGB LED (com. cathode, rgb) [package="5 mm [THT]"]
  LED6 = RGB LED (com. cathode, rgb) [package="5 mm [THT]"]
  LED7 = RGB LED (com. cathode, rgb) [package="5 mm [THT]"]
  SP1 = SPEAKER [package=pcb_mount_speaker]

nets:
  GND: Q3.E, Q4.E, Q5.E, LED3.common_cathode, Part1.GND, U1.GND, U2.GND, LED4.common_cathode, LED5.common_cathode, LED6.common_cathode, LED7.common_cathode, SP1.+
  N1: Q3.B, R1.Pin_0
  N2: Q3.C, D1.anode, M1.pin_2
  N3: R1.Pin_1, Part1.D9_PWM
  VCC: D1.cathode, M1.pin_1, D2.cathode, M2.pin_1, D3.cathode, M3.pin_1, Part1.5V, U1.MR, U1.VCC, U2.MR, U2.VCC
  N4: Q4.B, R2.Pin_0
  N5: Q4.C, D2.anode, M2.pin_2
  N6: R2.Pin_1, Part1.D10_PWM/SS
  N7: Q5.B, R3.Pin_0
  N8: Q5.C, D3.anode, M3.pin_2
  N9: R3.Pin_1, Part1.D11_PWM/MOSI
  N10: R10.Pin_0, LED3.blue_anode
  N11: R10.Pin_1, U1.Q2
  N12: R11.Pin_0, LED3.red_anode
  N13: R11.Pin_1, U1.Q0
  N14: R12.Pin_0, LED3.green_anode
  N15: R12.Pin_1, U1.Q1
  N16: Part1.D2, U1.DS
  N17: Part1.D3_PWM, U1.OE, U2.OE
  N18: Part1.D4, U1.ST_CP, U2.ST_CP
  N19: Part1.D5_PWM, SP1.-
  N20: Part1.D7, U1.SH_CP, U2.SH_CP
  N21: U1.Q3, R14.Pin_1
  N22: U1.Q4, R13.Pin_1
  N23: U1.Q5, R15.Pin_1
  N24: U1.Q6, R20.Pin_1
  N25: U1.Q7, R19.Pin_1
  N26: U1.Q7', U2.DS
  N27: U2.Q1, R17.Pin_1
  N28: U2.Q2, R16.Pin_1
  N29: U2.Q4, R23.Pin_1
  N30: U2.Q5, R22.Pin_1
  N31: U2.Q6, R24.Pin_1
  N32: U2.Q0, R21.Pin_1
  N33: R13.Pin_0, LED4.green_anode
  N34: R14.Pin_0, LED4.red_anode
  N35: R15.Pin_0, LED4.blue_anode
  N36: R16.Pin_0, LED6.green_anode
  N37: R17.Pin_0, LED6.red_anode
  N38: R18.Pin_0, LED6.blue_anode
  N39: R19.Pin_0, LED5.green_anode
  N40: R20.Pin_0, LED5.red_anode
  N41: R21.Pin_0, LED5.blue_anode
  N42: R22.Pin_0, LED7.green_anode
  N43: R23.Pin_0, LED7.red_anode
  N44: R24.Pin_0, LED7.blue_anode
