# Fritzing sketch fountain_rpi (saved by Fritzing 0.9.3b)
breadboards: 1

parts:
  Raspberry_Pi_1 = Raspberry Pi 3 [part_number=RPI-3-V1.2]
  Q3 = NPN-Transistor [package="TO92 [THT]"]
  R1 = Resistor [tolerance=±5% resistance=330 package="2512 [SMD]"]
  D1 = Rectifier Diode [package="Melf DO-213 AA [SMD]"]
  M1 = DC Motor
  Q4 = NPN-Transistor [package="TO92 [THT]"]
  R2 = Resistor [tolerance=±5% resistance=330 package="2512 [SMD]"]
  D2 = Rectifier Diode [package="Melf DO-213 AA [SMD]"]
  M2 = DC Motor
  Q5 = NPN-Transistor [package="TO92 [THT]"]
  R3 = Resistor [tolerance=±5% resistance=330 package="2512 [SMD]"]
  D3 = Rectifier Diode [package="Melf DO-213 AA [SMD]"]
  M3 = DC Motor
  LED1 = RGB LED (com. cathode, rgb) [package="5 mm [THT]"]
  R4 = Resistor [tolerance=±5% resistance=220 package="2512 [SMD]"]
  R5 = Resistor [tolerance=±5% resistance=220 package="2512 [SMD]"]
  R6 = Resistor [tolerance=±5% resistance=220 package="2512 [SMD]"]
  R7 = Resistor [tolerance=±5% resistance=220 package="2512 [SMD]"]
  R8 = Resistor [tolerance=±5% resistance=220 package="2512 [SMD]"]
  R9 = Resistor [tolerance=±5% resistance=220 package="2512 [SMD]"]
  LED2 = RGB LED (com. cathode, rgb) [package="5 mm [THT]"]
  R10 = Resistor [tolerance=±5% resistance=220 package="2512 [SMD]"]
  R11 = Resistor [tolerance=±5% resistance=220 package="2512 [SMD]"]
  R12 = Resistor [tolerance=±5% resistance=220 package="2512 [SMD]"]
  LED3 = RGB LED (com. cathode, rgb) [package="5 mm [THT]"]

nets:
  N1: Raspberry_Pi_1.GPIO4, Raspberry_Pi_1.GPIO14, R1.Pin_1
  N2: Raspberry_Pi_1.GPIO17, Raspberry_Pi_1.GPIO18, R2.Pin_1
  N3: Raspberry_Pi_1.GPIO27, Raspberry_Pi_1.GND, Raspberry_Pi_1.GPIO5, Raspberry_Pi_1.GPIO13, Q3.E, Q4.E, Q5.E, R3.Pin_1, LED1.common_cathode, R8.Pin_1, LED2.common_cathode, R11.Pin_1, LED3.common_cathode
  N4: Raspberry_Pi_1.GPIO6, R7.Pin_1
  N5: Raspberry_Pi_1.GPIO26, Raspberry_Pi_1.GPIO20, R10.Pin_1
  N6: Raspberry_Pi_1.GPIO16, R12.Pin_1
  N7: Raspberry_Pi_1.GPIO12, R9.Pin_1
  N8: Raspberry_Pi_1.GPIO25, R6.Pin_1
  N9: Raspberry_Pi_1.GPIO24, R5.Pin_1
  N10: Raspberry_Pi_1.GPIO23, R4.Pin_1
  N11: Raspberry_Pi_1.5V, D1.cathode, M1.pin_1, D2.cathode, M2.pin_1, D3.cathode, M3.pin_1
  N12: Q3.B, R1.Pin_0
  N13: Q3.C, D1.anode, M1.pin_2
  N14: Q4.B, R2.Pin_0
  N15: Q4.C, D2.anode, M2.pin_2
  N16: Q5.B, R3.Pin_0
  N17: Q5.C, D3.anode, M3.pin_2
  N18: LED1.red_anode, R4.Pin_0
  N19: LED1.green_anode, R5.Pin_0
  N20: LED1.blue_anode, R6.Pin_0
  N21: R7.Pin_0, LED2.blue_anode
  N22: R8.Pin_0, LED2.red_anode
  N23: R9.Pin_0, LED2.green_anode
  N24: R10.Pin_0, LED3.blue_anode
  N25: R11.Pin_0, LED3.red_anode
  N26: R12.Pin_0, LED3.green_anode
